# Fritzing sketch PN532 (saved by Fritzing 0.9.10b)

parts:
  Componente1 = PN532 Elechouse RFID NFC Module V3
  Componente2 = Arduino Uno (Rev3) - ICSP

nets:
  GND: Componente1.GND, Componente2.GND
  VCC: Componente1.VCC, Componente2.5V
  N1: Componente1.SDA, Componente2.A4/SDA
  N2: Componente1.SCL, Componente2.A5/SCL

custom parts:
  PN532 Elechouse RFID NFC Module V3: NFC is a popular technology in recent years. We often heard this work while smart phone company such as Samsung or HTC introduces their latest high-end phones. Almost all the high-end phone in the market support NFC. Near field communication (NFC) is a set of standards for smart phones and similar devices to establish radio communication with each other by touching them together or bringing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
